// Logisim project CPU.circ as structural Verilog: 5 circuits, main circuit implementation
module implementation (
  output [7:0] print_R0,
  output [7:0] print_R1,
  output halt
);

  wire and_2_out, and_3_out, and_4_out, and_5_out, BusOut, clk, comparator_1_eq, comparator_2_eq, ds, IRin,
       IRout, MARin, MDRout, MRead, not_1_out, not_2_out, not_3_out, Num1out, OffsetOut, PCin, PCout, R0in,
       R0out, R1in, R1out, Rdsin, Rdsout, Rsout, s, Xin, Zin, Zout;
  wire [1:0] aluctrl_1_aluctrl, demultiplexer_1_out0;
  wire [2:0] Imm;
  wire [3:0] Offset;
  wire [4:0] State;
  wire [7:0] alu_1_alu_out, bit_extender_1_out, controlled_buffer_1_out, controlled_buffer_3_out, IR, MAR_q,
       MDR_q, Mem_dout, multiplexer_1_out, multiplexer_2_out, Num1_q, PC, X_q, Z_q;

  RAM Mem (.addr(MAR_q), .oe(MRead), .clk(clk), .dout(Mem_dout));  // open: we, din
  Register #(.trigger("high")) MDR (.D(Mem_dout), .clk(clk), .Q(MDR_q));  // open: en, clr
  assign controlled_buffer_1_out = MDRout ? MDR_q : 8'bz;  // Controlled_Buffer controlled_buffer_1
  Register u_PC (.D(controlled_buffer_1_out), .en(PCin), .clk(clk), .Q(PC));  // open: clr
  assign controlled_buffer_1_out = PCout ? PC : 8'bz;  // Controlled_Buffer controlled_buffer_2
  Register MAR (.D(controlled_buffer_1_out), .en(MARin), .clk(clk), .Q(MAR_q));  // open: clr
  Comparator comparator_1 (.a(PC), .b(8'hf), .eq(comparator_1_eq));  // open: gt, lt
  Comparator comparator_2 (.a(IR), .b({8{1'b0}}), .eq(comparator_2_eq));  // open: gt, lt
  Statectrl statectrl_1 (.OPcode(IR[7:4]), .clk(clk), .currState(State));
  Register #(.trigger("high")) u_IR (.D(controlled_buffer_1_out), .en(IRin), .clk(clk), .Q(IR));  // open: clr
  Multiplexer #(.width(8)) multiplexer_1 (
    .in0({{5{1'b0}}, Imm}), .in1(bit_extender_1_out), .out(multiplexer_1_out), .sel(OffsetOut));
  Clock u_clk (.out(clk));
  and and_1 (halt, comparator_1_eq, comparator_2_eq);
  Register R0 (.D(controlled_buffer_1_out), .en(R0in), .clk(clk), .Q(print_R0));  // open: clr
  assign controlled_buffer_3_out = IRout ? multiplexer_1_out : 8'bz;  // Controlled_Buffer controlled_buffer_3
  Multiplexer #(.width(8)) multiplexer_2 (
    .in0(controlled_buffer_3_out), .in1(controlled_buffer_1_out), .out(multiplexer_2_out), .sel(BusOut));
  assign controlled_buffer_1_out = R0out ? print_R0 : 8'bz;  // Controlled_Buffer controlled_buffer_4
  ALUctrl aluctrl_1 (.State(State), .OPcode(IR[7:4]), .ALUCtrl(aluctrl_1_aluctrl));
  ROM #(.addrWidth(5), .dataWidth(16)) CtrlSignals (
    .addr(State),
    .data({OffsetOut, BusOut, MRead, Xin, MARin, Zout, Zin, MDRout, Rsout, Num1out, Rdsout, Rdsin, IRout, IRin, PCout, PCin}));
  Demultiplexer #(.disabled("Z"), .select(4), .tristate("true"), .width(4)) demultiplexer_1 (
    .out0({ds, s, demultiplexer_1_out0}), .out1({ds, s, demultiplexer_1_out0}),
    .out2({ds, s, demultiplexer_1_out0}), .out3({ds, Imm}), .out4({ds, s, demultiplexer_1_out0}),
    .out15(Offset), .in(IR[3:0]), .sel(IR[7:4]));  // open: out5, out6, out7, out8, out9, out10, out11, out12, out13, out14
  Register R1 (.D(controlled_buffer_1_out), .en(R1in), .clk(clk), .Q(print_R1));  // open: clr
  assign controlled_buffer_1_out = R1out ? print_R1 : 8'bz;  // Controlled_Buffer controlled_buffer_5
  assign bit_extender_1_out = {{4{Offset[3]}}, Offset};  // Bit_Extender bit_extender_1
  Register Num1 (.D(8'h1), .clk(clk), .Q(Num1_q));  // open: en, clr
  Register X (.D(controlled_buffer_1_out), .en(Xin), .clk(clk), .Q(X_q));  // open: clr
  assign controlled_buffer_1_out = Num1out ? Num1_q : 8'bz;  // Controlled_Buffer controlled_buffer_6
  ALU alu_1 (.A(X_q), .B(multiplexer_2_out), .ALU_in(aluctrl_1_aluctrl), .ALU_out(alu_1_alu_out));
  Register Z (.D(alu_1_alu_out), .en(Zin), .clk(clk), .Q(Z_q));  // open: clr
  assign controlled_buffer_1_out = Zout ? Z_q : 8'bz;  // Controlled_Buffer controlled_buffer_7
  not not_1 (not_1_out, ds);
  not not_2 (not_2_out, s);
  not not_3 (not_3_out, ds);
  and and_2 (and_2_out, Rdsout, not_1_out);
  and and_3 (and_3_out, Rsout, not_2_out);
  and and_4 (and_4_out, Rdsout, ds);
  and and_5 (and_5_out, Rsout, s);
  and and_6 (R0in, Rdsin, not_3_out);
  and and_7 (R1in, Rdsin, ds);
  or or_1 (R0out, and_2_out, and_3_out);
  or or_2 (R1out, and_4_out, and_5_out);

  // Other names for the same wires on the sheet: OPcode[3:0] = IR[7:4]; R0[7:0] = print_R0; R1[7:0] = print_R1

  // Notes on the sheet:
  //   contents of CtrlSignals (hex, n*v repeats v):
  //   3802 6240 2401 104 1020 4280 410 1020 208 410 1002 8208 401 2880 3020 4300 410
endmodule

module ALU (
  input  [7:0] A,
  input  [7:0] B,
  input  [1:0] ALU_in,
  output [7:0] ALU_out
);

  wire [7:0] adder_1_out, multiplier_1_out, nand_1_out, subtractor_1_out;

  Adder adder_1 (.a(A), .b(B), .out(adder_1_out));  // open: cin, cout
  Subtractor subtractor_1 (.a(A), .b(B), .out(subtractor_1_out));  // open: bin, bout
  Multiplier multiplier_1 (.a(A), .b(B), .out(multiplier_1_out));  // open: cin, cout
  assign nand_1_out = ~(B & A);  // NAND_Gate nand_1, 8 bits wide
  Multiplexer #(.select(2), .width(8)) multiplexer_1 (
    .in0(nand_1_out), .in1(multiplier_1_out), .in2(subtractor_1_out), .in3(adder_1_out), .out(ALU_out),
    .sel(ALU_in));
endmodule

module Statectrl (
  input  [3:0] OPcode,
  input  clk,
  output [4:0] currState
);

  wire [4:0] statecomb_1_nextstate, Y0_q;

  D_Flip_Flop Y4 (.D(statecomb_1_nextstate[4]), .clk(clk), .Q(Y0_q[4]));  // open: Qn, preset, reset
  D_Flip_Flop Y3 (.D(statecomb_1_nextstate[3]), .clk(clk), .Q(Y0_q[3]));  // open: Qn, preset, reset
  D_Flip_Flop Y2 (.D(statecomb_1_nextstate[2]), .clk(clk), .Q(Y0_q[2]));  // open: Qn, preset, reset
  Statecomb statecomb_1 (.State(Y0_q), .OP(OPcode), .NextState(statecomb_1_nextstate), .Output(currState));
  D_Flip_Flop Y1 (.D(statecomb_1_nextstate[1]), .clk(clk), .Q(Y0_q[1]));  // open: Qn, preset, reset
  D_Flip_Flop Y0 (.D(statecomb_1_nextstate[0]), .clk(clk), .Q(Y0_q[0]));  // open: Qn, preset, reset
endmodule

module Statecomb (
  input  [4:0] State,
  input  [3:0] OP,
  output [4:0] NextState,
  output [4:0] Output
);

  wire and_1_out, and_2_out, and_3_out, and_4_out, and_5_out, and_6_out, and_7_out, and_8_out, and_9_out,
       and_10_out, and_11_out, and_12_out, and_13_out, and_14_out, and_15_out, and_16_out, and_17_out,
       and_18_out, and_19_out, and_20_out, and_21_out, and_22_out, and_23_out, and_24_out, and_25_out,
       and_26_out, and_27_out, and_28_out, and_29_out, and_30_out, and_31_out, and_32_out, and_33_out,
       and_34_out, and_35_out, and_36_out, and_37_out, not_1_out, not_2_out, not_3_out, not_4_out, not_5_out,
       not_6_out, not_7_out, not_8_out, not_9_out;

  not not_1 (not_1_out, State[4]);
  not not_2 (not_2_out, State[3]);
  not not_3 (not_3_out, State[2]);
  not not_4 (not_4_out, State[1]);
  not not_5 (not_5_out, State[0]);
  not not_6 (not_6_out, OP[3]);
  not not_7 (not_7_out, OP[2]);
  not not_8 (not_8_out, OP[1]);
  not not_9 (not_9_out, OP[0]);
  and and_1 (and_1_out, State[3], State[2], State[1], State[0]);
  and and_2 (and_2_out, State[4], State[0]);
  and and_3 (and_3_out, State[4], State[1]);
  and and_4 (and_4_out, State[4], State[2]);
  and and_5 (and_5_out, State[4], State[3]);
  and and_6 (and_6_out, not_1_out, not_2_out, State[2], State[1], State[0]);
  and and_7 (and_7_out, State[3], not_3_out, not_5_out);
  and and_8 (and_8_out, State[3], not_3_out, State[1]);
  and and_9 (and_9_out, State[3], State[2], not_4_out, State[0]);
  and and_10 (and_10_out, State[3], State[1], not_5_out);
  and and_11 (and_11_out, State[4], State[3]);
  and and_12 (and_12_out, not_1_out, not_2_out, State[1], State[0], not_6_out, not_7_out, OP[1], not_9_out);
  and and_13 (and_13_out, not_1_out, not_2_out, State[1], State[0], OP[3], OP[2], OP[1], OP[0]);
  and and_14 (and_14_out, not_1_out, not_3_out, State[1], State[0], not_6_out, not_7_out);
  and and_15 (and_15_out, not_1_out, not_3_out, State[1], State[0], not_6_out, not_8_out, not_9_out);
  and and_16 (and_16_out, not_2_out, State[2], not_4_out);
  and and_17 (and_17_out, not_1_out, State[3], not_3_out, State[1], State[0]);
  and and_18 (and_18_out, State[2], not_4_out, State[0]);
  and and_19 (and_19_out, State[3], State[2], State[1], not_5_out);
  and and_20 (and_20_out, State[4], State[2]);
  and and_21 (and_21_out, not_1_out, not_2_out, not_4_out, State[0]);
  and and_22 (and_22_out, not_3_out, State[1], not_5_out);
  and and_23 (and_23_out, not_1_out, State[2], not_4_out, State[0]);
  and and_24 (and_24_out, State[3], State[1], not_5_out);
  and and_25 (and_25_out, State[4], State[1]);
  and and_26 (and_26_out, not_2_out, not_3_out, State[1], OP[1], OP[0]);
  and and_27 (and_27_out, not_2_out, not_3_out, State[1], OP[2], OP[0]);
  and and_28 (and_28_out, not_2_out, not_3_out, State[1], OP[2], OP[1]);
  and and_29 (and_29_out, not_2_out, not_3_out, State[1], OP[3]);
  and and_30 (and_30_out, not_1_out, not_3_out, not_5_out);
  and and_31 (and_31_out, not_1_out, not_2_out, not_4_out, not_5_out);
  and and_32 (and_32_out, not_1_out, State[3], State[1], not_5_out);
  and and_33 (and_33_out, State[4], State[0]);
  and and_34 (and_34_out, not_1_out, not_2_out, not_3_out, State[1], not_6_out, OP[1]);
  and and_35 (and_35_out, not_1_out, not_2_out, not_3_out, State[1], OP[3], not_7_out);
  and and_36 (and_36_out, not_1_out, not_2_out, not_3_out, State[1], OP[2], not_8_out, OP[0]);
  and and_37 (and_37_out, not_1_out, not_2_out, not_3_out, State[1], OP[3], not_9_out);
  or or_1 (NextState[4], and_1_out, and_2_out, and_3_out, and_4_out, and_5_out);
  or or_2 (NextState[3], and_6_out, and_7_out, and_8_out, and_9_out, and_10_out, and_11_out, and_12_out, and_13_out);
  or or_3 (NextState[2], and_14_out, and_15_out, and_16_out, and_17_out, and_18_out, and_19_out, and_20_out);
  or or_4 (NextState[1], and_21_out, and_22_out, and_23_out, and_24_out, and_25_out, and_26_out, and_27_out, and_28_out, and_29_out);
  or or_5 (NextState[0], and_30_out, and_31_out, and_32_out, and_33_out, and_34_out, and_35_out, and_36_out, and_37_out);

  assign Output = State;
endmodule

module ALUctrl (
  input  [4:0] State,
  input  [3:0] OPcode,
  output [1:0] ALUCtrl
);

  wire and_1_out, and_2_out, and_3_out, and_4_out, and_5_out, and_6_out, and_7_out, and_8_out, and_9_out,
       not_1_out, not_2_out, not_3_out, not_4_out, not_5_out, not_6_out, not_7_out, not_8_out, not_9_out;

  not not_1 (not_1_out, State[4]);
  not not_2 (not_2_out, State[3]);
  not not_3 (not_3_out, State[2]);
  not not_4 (not_4_out, State[1]);
  not not_5 (not_5_out, State[0]);
  not not_6 (not_6_out, OPcode[3]);
  not not_7 (not_7_out, OPcode[2]);
  not not_8 (not_8_out, OPcode[1]);
  not not_9 (not_9_out, OPcode[0]);
  and and_1 (and_1_out, not_1_out, State[3], not_3_out, not_4_out, not_5_out);
  and and_2 (and_2_out, not_1_out, not_2_out, not_3_out, not_4_out, State[0]);
  and and_3 (and_3_out, not_1_out, State[3], State[1], State[0]);
  and and_4 (and_4_out, not_1_out, not_2_out, not_4_out, State[0], not_6_out, not_7_out, not_8_out, OPcode[0]);
  and and_5 (and_5_out, not_1_out, not_2_out, not_4_out, State[0], not_6_out, OPcode[2], not_8_out, not_9_out);
  and and_6 (and_6_out, not_1_out, State[3], not_3_out, not_4_out, not_5_out);
  and and_7 (and_7_out, not_1_out, not_2_out, not_3_out, not_4_out, State[0]);
  and and_8 (and_8_out, not_1_out, State[3], State[1], State[0]);
  and and_9 (and_9_out, not_1_out, not_2_out, not_4_out, State[0], not_6_out, not_7_out, not_8_out, OPcode[0]);
  or or_1 (ALUCtrl[1], and_1_out, and_2_out, and_3_out, and_4_out, and_5_out);
  or or_2 (ALUCtrl[0], and_6_out, and_7_out, and_8_out, and_9_out);
endmodule
